# Fritzing sketch simonSays (saved by Fritzing 0.9.3b)
breadboards: 1

parts:
  Part1 = Arduino Uno (Rev3)
  S2 = Momentary Switch [package=ksa_sealed_tac_switch]
  S3 = Momentary Switch [package=ksa_sealed_tac_switch]
  S4 = Momentary Switch [package=ksa_sealed_tac_switch]
  LED1 = smd LED [color="Blue (430nm)" package="0805 [SMD]"]
  LED2 = smd LED [color="Red (633nm)" package="0805 [SMD]"]
  LED3 = smd LED [color="Yellow (585nm)" package="0805 [SMD]"]
  LED4 = smd LED [color="Green (555nm)" package="0805 [SMD]"]
  S1 = Momentary Switch [package=ksa_sealed_tac_switch]
  J1 = Piezo Speaker
  R1 = Resistor [tolerance=±5% resistance=100 package="2010 [SMD]"]
  R2 = Resistor [tolerance=±5% resistance=100 package="2010 [SMD]"]
  R3 = Resistor [tolerance=±5% resistance=100 package="2010 [SMD]"]
  R4 = Resistor [tolerance=±5% resistance=100 package="2010 [SMD]"]
  R5 = Resistor [tolerance=±5% resistance=220 package="2010 [SMD]"]
  R6 = Resistor [tolerance=±5% resistance=220 package="2010 [SMD]"]
  R7 = Resistor [tolerance=±5% resistance=220 package="2010 [SMD]"]
  R8 = Resistor [tolerance=±5% resistance=220 package="2010 [SMD]"]

nets:
  N1: Part1.D9_PWM, LED4.anode
  N2: Part1.D10_PWM/SS, LED3.anode
  N3: Part1.D11_PWM/MOSI, LED2.anode
  N4: Part1.D12/MISO, LED1.anode
  N5: Part1.GND, J1.pin1, R1.Pin_1, R2.Pin_1, R3.Pin_1, R4.Pin_1, R5.Pin_0, R6.Pin_0, R7.Pin_0, R8.Pin_0
  N6: Part1.D3_PWM, J1.pin2
  N7: Part1.D4, S4.2, R8.Pin_1
  N8: Part1.D5_PWM, S3.2, R7.Pin_1
  N9: Part1.D6_PWM, S2.2, R5.Pin_1
  N10: Part1.D7, S1.2, R6.Pin_1
  N11: Part1.5V, S2.3, S3.3, S4.3, S1.3
  N12: LED1.cathode, R3.Pin_0
  N13: LED2.cathode, R2.Pin_0
  N14: LED3.cathode, R1.Pin_0
  N15: LED4.cathode, R4.Pin_0
